# Fritzing sketch Magneto (saved by Fritzing 0.9.3b)
breadboards: 1

parts:
  Composant1 = Arduino Mega ADK (Rev3)
  Grove1 = Grove OLED 128x96
  Composant2 = Adafruit ADS1115 16Bit I2C ADC [part_number="Adafruit #1085"]
  Composant3 = Adafruit MicroSD card breakout board [part_number="Adafruit #254"]
  J1 = Screw terminal - 2 pins [package=THT]
  GPS1 = Adafruit Ultimate GPS Breakout
  J3 = Screw terminal - 2 pins [package=THT]
  J4 = Screw terminal - 2 pins [package=THT]
  Composant4 = Adafruit DS1307 RTC Breakout [part_number="Adafruit #264"]
  J5 = Screw terminal - 2 pins [package=THT]

nets:
  N1: Composant1.A0, J3.pin1, J4.pin2
  N2: Composant1.D21/SCL, Grove1.SCL, Composant2.SCL, Composant4.SCL
  N3: Composant1.D20/SDA, Grove1.SDA, Composant2.SDA, Composant4.SDA
  N4: Composant1.D19/RX1, GPS1.TX
  N5: Composant1.D18/TX1, GPS1.RX
  VCC: Composant1.5V, Grove1.VCC, Composant2.VDD, Composant3.VCC, GPS1.VIN, J3.pin2, Composant4.VCC
  GND: Composant1.GND, Grove1.GND, Composant2.ADDR, Composant2.GND, Composant3.GND, GPS1.GND, J4.pin1, Composant4.GND
  N6: Composant1.D50/MISO, Composant3.DO
  N7: Composant1.D51/MOSI, Composant3.DI
  N8: Composant1.D52/SCK, Composant3.CLK
  N9: Composant1.D53/SS, Composant3.CS
  N10: Composant2.AIN3, J1.pin2
  N11: Composant2.AIN2, J1.pin1
  N12: Composant2.AIN1, J5.pin2
  N13: Composant2.AIN0, J5.pin1

custom parts:
  Adafruit ADS1115 16Bit I2C ADC: For microcontrollers without an analog-to-digital converter or when you want a higher-precision ADC, the ADS1115 provides 16-bit precision at 860 samples/second over I2C. The chip can be configured as 4 single-ended input channels, or two differential channels. As a nice bonus, it even includes a programmable gain amplifier, up to x16, to help boost up smaller single/differential signals to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
  Adafruit MicroSD card breakout board: Not just a simple breakout board, this microSD adapter goes the extra mile - designed for ease of use. Onboard 5v->3v regulator provides 150mA for power-hungry cards 3v level shifting means you can use this with ease on either 3v or 5v systems Uses a proper level shifting chip, not resistors: less problems, and faster read/write access Use 3 or 4 digital pins to read and write 2Gb+ of storage!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
  Adafruit DS1307 RTC Breakout: This is a great battery-backed real time clock (RTC) that allows your microcontroller project to keep track of time even if it is reprogrammed, or if the power is lost. Perfect for datalogging, clock-building, time stamping, timers and alarms, etc. The DS1307 is the most popular RTC - but it requires 5V power to work (although we've used it with 5V power and 3.3V logic successfully) PCB &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
